# Fritzing sketch CaptainSmollett rev 1 (saved by Fritzing 0.9.3b)
circuit board: 7cm x 7cm
breadboards: 1

parts:
  2N7000_NPN = NPN-Transistor [package="TO92 [THT]"]
  10kΩ = Resistor [tolerance=±5% resistance=10k package=THT]
  49_9kΩ = Resistor [tolerance=±5% resistance=1k package=THT]
  10kΩ_2 = Resistor [tolerance=±5% resistance=10k package=THT]
  20kΩ = Resistor [tolerance=±5% resistance=10k package=THT]
  D1 = Zener Diode [part_number=1N4732A breakdown_voltage=3.6V package="300 mil [THT]"]
  1kΩ = Resistor [tolerance=±5% resistance=1k package=THT]
  330Ω = Resistor [tolerance=±5% resistance=330 package=THT]
  LM358 = LM 358 Dual Op-Amp [package="DIP8 [THT]"]
  GND = female pin header, 2 pins [form="♀ (female)"]
  Off = Trimmer Potentiometer [maximum_resistance=10kΩ package=THT]
  IN+ = female pin header, 1 pin [form="♀ (female)"]
  OUT+ = female pin header, 1 pin [form="♀ (female)"]
  IN- = female pin header, 1 pin [form="♀ (female)"]
  OUT- = female pin header, 1 pin [form="♀ (female)"]
  ACT4088 = MCP4725 [package=SOT23-6]
  R-OFF = Resistor [tolerance=±5% resistance=6.8k package=THT]
  10kΩ_3 = Resistor [tolerance=±5% resistance=10k package=THT]
  On = Trimmer Potentiometer [maximum_resistance=10kΩ package=THT]
  R-ON = Resistor [tolerance=±5% resistance=6.8k package=THT]
  10kΩ_4 = Resistor [tolerance=±5% resistance=10k package=THT]
  20kΩ_2 = Resistor [tolerance=±5% resistance=22k package=THT]
  RPi = female pin header, 4 pins [form="♀ (female)"]
  Reset = Pushbutton [package="[THT]"]
  D2 = Zener Diode [part_number=1N4732A breakdown_voltage=3.6V package="300 mil [THT]"]
  D3 = Zener Diode [part_number=1N4732A breakdown_voltage=3.6V package="300 mil [THT]"]
  D4 = Zener Diode [part_number=1N4732A breakdown_voltage=3.6V package="300 mil [THT]"]
  C100 = Capacitor Polarized [package=cpol-radial-100uf-25v]
  1k_Ω = Resistor [tolerance=±5% resistance=330 package=THT]
  Green = LED - 3mm [color="Green (565nm)" package="3 mm [THT]"]
  1k_Ω_2 = Resistor [tolerance=±5% resistance=330 package=THT]
  Red = LED - 3mm [color="Green (565nm)" package="3 mm [THT]"]
  220Ω = Resistor [tolerance=±5% resistance=330 package=THT]
  Blue = LED - 3mm [color="Green (565nm)" package="3 mm [THT]"]
  Zener = Zener Diode [part_number=1N4732A breakdown_voltage=3.6V package="300 mil [THT]"]
  9_5kΩ = Resistor [tolerance=±5% resistance=1k package=THT]
  C10 = Capacitor Polarized [package=cpol-radial-100uf-25v]
  L1 = Inductor [package="400 mil [THT]"]
  Relay = female pin header, 5 pins [form="♀ (female)"]
  5v = female pin header, 5 pins [form="♀ (female)"]
  C22 = Capacitor Polarized [package=cpol-radial-10uf-25v]
  C22_2 = Capacitor Polarized [package=cpol-radial-10uf-25v]

nets:
  N1: 2N7000_NPN.E, 2N7000_NPN.B, 10kΩ.Pin_1, 10kΩ_2.Pin_0, 1kΩ.Pin_1, 330Ω.Pin_0, LM358.connector3, GND.pin1, IN-.pin1, OUT-.pin1, ACT4088.VSS, 10kΩ_3.Pin_1, 10kΩ_4.Pin_1, RPi.pin4, Reset.Pin_3, Reset.Pin_4, C100.-, Green.cathode, Red.cathode, Blue.cathode, 9_5kΩ.Pin_1
  N2: 2N7000_NPN.C, 5v.pin1
  N3: 10kΩ.Pin_0, 20kΩ_2.Pin_0, RPi.pin2
  N4: 49_9kΩ.Pin_0, ACT4088.VOUT, 9_5kΩ.Pin_0
  N5: 49_9kΩ.Pin_1, LM358.connector1, LM358.connector5, OUT+.pin1, L1.pin_0, Relay.pin1, Relay.pin5, C22.+
  N6: 10kΩ_2.Pin_1, 20kΩ.Pin_0, D2.anode, D3.cathode
  N7: 20kΩ.Pin_1, D4.cathode
  N8: D1.cathode, 20kΩ_2.Pin_1
  N9: D1.anode, LM358.connector6, 1k_Ω_2.Pin_1
  N10: 1kΩ.Pin_0, 330Ω.Pin_1, D2.cathode, C100.+
  N11: LM358.connector0, D4.anode, 1k_Ω.Pin_1
  N12: LM358.connector2, R-ON.Pin_0, 10kΩ_4.Pin_0
  N13: LM358.connector4, R-OFF.Pin_0, 10kΩ_3.Pin_0
  N14: LM358.connector7, GND.pin2, Off.leg1, IN+.pin1, ACT4088.SCL, On.leg1, C10.+
  N15: Off.wiper, R-OFF.Pin_1
  N16: ACT4088.VDD, C22_2.-
  N17: ACT4088.SDA, Zener.cathode, C22_2.+
  N18: On.wiper, R-ON.Pin_1
  N19: RPi.pin1, D3.anode
  N20: RPi.pin3, 220Ω.Pin_1, Relay.pin4
  N21: 1k_Ω.Pin_0, Green.anode
  N22: 1k_Ω_2.Pin_0, Red.anode
  N23: 220Ω.Pin_0, Blue.anode
  N24: Zener.anode, C10.-, C22.-

notes:
  AditNW
  Buck Converter
  Output
  Input
  GND
  5V
  Capt Smollett rev 1
  G
  10kΩ
