# Fritzing sketch JimHawkins2 (saved by Fritzing 0.9.3b)
circuit board: 6.6cm x 13cm
breadboards: 1

parts:
  Raspberry_Pi_2 = Raspberry Pi 3 [part_number=RPI-3-V1.2]
  1307 = DS1307 [package=THT]
  OSC1 = CRYSTAL - kHz [frequency="32 kHz"]
  + = female pin header, 2 pins [form="♀ (female)"]
  - = female pin header, 1 pin [form="♀ (female)"]
  1 = female pin header, 4 pins [form="♀ (female)"]
  Buttons = female pin header, 4 pins [form="♀ (female)"]
  R10k3 = Resistor [tolerance=±5% resistance=10k package=THT]
  R10k2 = Resistor [tolerance=±5% resistance=10k package=THT]
  R10k1 = Resistor [tolerance=±5% resistance=10k package=THT]
  C10nF3 = Capacitor [package=cap-pth-large]
  C10nF2 = Capacitor [package=cap-pth-large]
  C10nF1 = Capacitor [package=cap-pth-large]
  R1k = Resistor [tolerance=±5% resistance=10k package=THT]
  R1k_2 = Resistor [tolerance=±5% resistance=10k package=THT]
  R1k_3 = Resistor [tolerance=±5% resistance=10k package=THT]
  C10nF6 = Capacitor [package=cap-pth-large]
  R1k_4 = Resistor [tolerance=±5% resistance=10k package=THT]
  SLC = female pin header, 1 pin [form="♀ (female)"]
  SDA = female pin header, 1 pin [form="♀ (female)"]
  3V = female pin header, 1 pin [form="♀ (female)"]
  2n7000 = MOSFET-NCHANNEL [package=to-92]
  ARD = female pin header, 4 pins [form="♀ (female)"]
  2 = female pin header, 4 pins [form="♀ (female)"]
  LCD = female pin header, 4 pins [form="♀ (female)"]
  2n7000_2 = MOSFET-NCHANNEL [package=to-92]
  R4_7k = Resistor [tolerance=±5% resistance=10k package=THT]
  R4_7k_2 = Resistor [tolerance=±5% resistance=10k package=THT]
  R4_7k_3 = Resistor [tolerance=±5% resistance=10k package=THT]
  R4_7k_4 = Resistor [tolerance=±5% resistance=10k package=THT]
  3V_I2C = female pin header, 4 pins [form="♀ (female)"]
  3 = female pin header, 4 pins [form="♀ (female)"]
  2_2 = female pin header, 4 pins [form="♀ (female)"]
  1_2 = female pin header, 4 pins [form="♀ (female)"]
  5V = female pin header, 1 pin [form="♀ (female)"]
  GND = female pin header, 1 pin [form="♀ (female)"]
  GND_2 = female pin header, 1 pin [form="♀ (female)"]
  5V_2 = female pin header, 1 pin [form="♀ (female)"]
  D1 = Rectifier Diode [part_number=1N4001 package="300 mil [THT]"]
  RED = LED - 3mm [color="Red (633nm)" package="3 mm [THT]"]
  R220 = Resistor [tolerance=±5% resistance=10k package=THT]
  GND_3 = female pin header, 12 pins [form="♀ (female)"]
  3_3v = female pin header, 12 pins [form="♀ (female)"]
  P10 = female pin header, 1 pin [form="♀ (female)"]
  P8 = female pin header, 1 pin [form="♀ (female)"]
  P12 = female pin header, 1 pin [form="♀ (female)"]
  R1k_5 = Resistor [tolerance=±5% resistance=10k package=THT]
  R1k_6 = Resistor [tolerance=±5% resistance=10k package=THT]
  R1k_7 = Resistor [tolerance=±5% resistance=10k package=THT]
  P40 = female pin header, 1 pin [form="♀ (female)"]
  P38 = female pin header, 1 pin [form="♀ (female)"]
  P36 = female pin header, 1 pin [form="♀ (female)"]
  3_3V = female pin header, 1 pin [form="♀ (female)"]
  GND_4 = female pin header, 1 pin [form="♀ (female)"]
  GND_5 = female pin header, 1 pin [form="♀ (female)"]
  D2 = Rectifier Diode [part_number=1N4001 package="300 mil [THT]"]
  R1k_8 = Resistor [tolerance=±5% resistance=10k package=THT]
  G_3V_I/O = female pin header, 4 pins [form="♀ (female)"]
  2n7000_3 = MOSFET-NCHANNEL [package=to-92]
  2n7000_4 = MOSFET-NCHANNEL [package=to-92]
  R10k = Resistor [tolerance=±5% resistance=10k package=THT]
  R10k_2 = Resistor [tolerance=±5% resistance=10k package=THT]
  R10k_3 = Resistor [tolerance=±5% resistance=10k package=THT]
  R10k_4 = Resistor [tolerance=±5% resistance=10k package=THT]
  5_GND = female pin header, 4 pins [form="♀ (female)"]
  Zen = Zener Diode [part_number=1N4732A breakdown_voltage=3.6V package="300 mil [THT]"]
  Zen_2 = Zener Diode [part_number=1N4732A breakdown_voltage=3.6V package="300 mil [THT]"]
  Zen_3 = Zener Diode [part_number=1N4732A breakdown_voltage=3.6V package="300 mil [THT]"]
  Zen_4 = Zener Diode [part_number=1N4732A breakdown_voltage=3.6V package="300 mil [THT]"]
  Zen_5 = Zener Diode [part_number=1N4732A breakdown_voltage=3.6V package="300 mil [THT]"]
  Zen_6 = Zener Diode [part_number=1N4732A breakdown_voltage=3.6V package="300 mil [THT]"]
  Zen_7 = Zener Diode [part_number=1N4732A breakdown_voltage=3.6V package="300 mil [THT]"]
  Zen_8 = Zener Diode [part_number=1N4732A breakdown_voltage=3.6V package="300 mil [THT]"]
  R10k_5 = Resistor [tolerance=±5% resistance=10k package=THT]
  R10k_6 = Resistor [tolerance=±5% resistance=10k package=THT]
  R10k_7 = Resistor [tolerance=±5% resistance=10k package=THT]
  R10k_8 = Resistor [tolerance=±5% resistance=10k package=THT]
  R10k4 = Resistor [tolerance=±5% resistance=10k package=THT]

nets:
  3V3: Raspberry_Pi_2.3v3, Raspberry_Pi_2.3V3, Buttons.pin1, 3V.pin1, 2n7000.S, 2n7000_2.S, R4_7k_3.Pin_1, R4_7k_4.Pin_1, 3V_I2C.pin2, 3.pin2, 2_2.pin2, 1_2.pin2, GND_3.pin1, GND_3.pin12, 3_3v.pin1, 3_3v.pin12, 3_3V.pin1, G_3V_I/O.pin2, 2n7000_3.S, 2n7000_4.S, R10k.Pin_0, R10k_3.Pin_1
  N1: Raspberry_Pi_2.GPIO2, SDA.pin1, 2n7000.D, R4_7k_4.Pin_0, 3V_I2C.pin3, 3.pin3, 2_2.pin3, 1_2.pin3
  N2: Raspberry_Pi_2.GPIO3, SLC.pin1, 2n7000_2.D, R4_7k_3.Pin_0, 3V_I2C.pin4, 3.pin4, 2_2.pin4, 1_2.pin4
  N3: Raspberry_Pi_2.GND, 1307.0V, -.pin1, 1.pin1, R10k3.Pin_0, R10k2.Pin_0, R10k1.Pin_0, C10nF3.1, C10nF2.1, C10nF1.1, C10nF6.1, ARD.pin1, 2.pin1, LCD.pin1, 3V_I2C.pin1, 3.pin1, 2_2.pin1, 1_2.pin1, GND.pin1, GND_2.pin1, RED.cathode, GND_3.pin2, GND_3.pin11, 3_3v.pin2, 3_3v.pin11, GND_4.pin1, GND_5.pin1, G_3V_I/O.pin1, 5_GND.pin1, Zen.anode, Zen_2.anode, Zen_3.anode, Zen_4.anode, Zen_5.anode, Zen_6.anode, Zen_7.anode, Zen_8.anode, R10k_5.Pin_0, R10k_6.Pin_0, R10k_7.Pin_0, R10k_8.Pin_0, R10k4.Pin_0
  N4: Raspberry_Pi_2.GPIO5, R1k_8.Pin_1
  N5: Raspberry_Pi_2.GPIO6, R1k_2.Pin_1
  N6: Raspberry_Pi_2.GPIO13, R1k.Pin_1
  N7: Raspberry_Pi_2.GPIO19, 2n7000_4.D, R10k_3.Pin_0
  N8: Raspberry_Pi_2.GPIO26, 2n7000_3.D, R10k.Pin_1
  N9: Raspberry_Pi_2.GPIO21, P40.pin1
  N10: Raspberry_Pi_2.GPIO20, P38.pin1
  N11: Raspberry_Pi_2.GPIO16, P36.pin1
  N12: Raspberry_Pi_2.GPIO7, R1k_7.Pin_0
  N13: Raspberry_Pi_2.GPIO8, R1k_6.Pin_0
  N14: Raspberry_Pi_2.GPIO25, R1k_5.Pin_0
  N15: Raspberry_Pi_2.GPIO24, R1k_4.Pin_0
  N16: Raspberry_Pi_2.GPIO23, R1k_3.Pin_0
  N17: Raspberry_Pi_2.GPIO18, P12.pin1, 5_GND.pin4, Zen_2.cathode
  N18: Raspberry_Pi_2.GPIO15, P10.pin1, 5_GND.pin3, Zen.cathode
  N19: Raspberry_Pi_2.GPIO14, R220.Pin_0, P8.pin1
  N20: Raspberry_Pi_2.5V, 1307.+V, 1.pin2, C10nF6.2, 2.pin2, LCD.pin2, R4_7k.Pin_0, R4_7k_2.Pin_0, 5V.pin1, 5V_2.pin1, D1.cathode, D2.anode, R10k_2.Pin_0, R10k_4.Pin_1
  N21: 1307.X1_-_Crystal, OSC1.pin_1
  N22: 1307.X2_-_Crystal, OSC1.pin_0
  N23: 1307.Vbat_-_Backup_Supply, +.pin1, +.pin2
  N24: 1307.SDA_-_I2C_Data, 1.pin3, 2n7000.G, ARD.pin3, 2.pin3, LCD.pin3, R4_7k.Pin_1
  N25: 1307.SCL_-_I2C_Clock, 1.pin4, ARD.pin4, 2.pin4, LCD.pin4, 2n7000_2.G, R4_7k_2.Pin_1
  N26: Buttons.pin2, R10k1.Pin_1, C10nF1.2, R1k.Pin_0
  N27: Buttons.pin3, R10k2.Pin_1, C10nF2.2, R1k_2.Pin_0
  N28: Buttons.pin4, R10k3.Pin_1, C10nF3.2, R1k_8.Pin_0
  N29: R1k_3.Pin_1, GND_3.pin10, 3_3v.pin10, Zen_4.cathode, R10k_6.Pin_1
  N30: R1k_4.Pin_1, GND_3.pin9, 3_3v.pin9, Zen_5.cathode, R10k4.Pin_1
  N31: ARD.pin2, D2.cathode
  N32: D1.anode, 5_GND.pin2, Zen_3.cathode
  N33: RED.anode, R220.Pin_1
  N34: GND_3.pin3, 3_3v.pin3
  N35: GND_3.pin4, 3_3v.pin4
  N36: GND_3.pin5, 3_3v.pin5
  N37: GND_3.pin6, 3_3v.pin6, R1k_7.Pin_1, Zen_8.cathode, R10k_5.Pin_1
  N38: GND_3.pin7, 3_3v.pin7, R1k_6.Pin_1, Zen_7.cathode, R10k_7.Pin_1
  N39: GND_3.pin8, 3_3v.pin8, R1k_5.Pin_1, Zen_6.cathode, R10k_8.Pin_1
  N40: G_3V_I/O.pin3, 2n7000_3.G, R10k_2.Pin_1
  N41: G_3V_I/O.pin4, 2n7000_4.G, R10k_4.Pin_0

notes:
  CR2032
  AditNW
  G
  5V
  3V 1 2 3
  SCL
  5V I2C
  3.3V I2C
  Lvl Shift
  Jim Hawkins
